# Fritzing sketch cheme (saved by Fritzing 0.9.3b)

parts:
  Part1 = Arduino Mega ADK (Rev3)
  Part2 = Arduino Ethernet Shield (Rev3)
  ZS-042_RTC1 = ZS-042 RTC Module
  U1 = RFID RC522 SIP - 8 pins [chip_label="RFID RC522" package="SIP (Single Inline) [THT]"]
  J1 = Piezo Speaker

nets:
  N1: Part1.D21/SCL, ZS-042_RTC1.SCL
  N2: Part1.D20/SDA, ZS-042_RTC1.SDA
  N3: Part1.D50/MISO, U1.MISO
  N4: Part1.D51/MOSI, U1.MOSI
  N5: Part1.D52/SCK, U1.SCK
  N6: Part2.PWM_D9, U1.RST
  GND: Part2.GND, ZS-042_RTC1.GND, U1.GND, J1.pin1
  N7: Part2.PWM_D3, J1.pin2
  N8: Part2.D7, U1.NSS
  3V3: Part2.3V3, U1.VCC
  5V: Part2.5V, ZS-042_RTC1.VCC

custom parts:
  RFID RC522 SIP - 8 pins: A SIP stand-in part for RFID RC522 . With 8 pins on a 300 mil single inline package (SIP) footprint.
